# Fritzing sketch BLINK_2017 (saved by Fritzing 0.9.2b)
breadboards: 1

parts:
  R1 = Resistor [tolerance=±5% resistance=220 package=THT]
  R2 = Resistor [tolerance=±5% resistance=220 package=THT]
  LED1 = LED - 5mm [color="Red (633nm)" package="5 mm [THT]"]
  LED2 = LED - 5mm [color="Green (570nm)" package="5 mm [THT]"]
  Componente1 = Arduino Uno (Rev3)

nets:
  N1: R1.Pin_0, LED1.anode
  N2: R1.Pin_1, Componente1.D3_PWM
  N3: R2.Pin_0, LED2.anode
  N4: R2.Pin_1, Componente1.D9_PWM
  N5: LED1.cathode, LED2.cathode, Componente1.GND

notes:
  Resistenze LED 220 ohm
