# Fritzing sketch DIGITAL_IO_2017 (saved by Fritzing 0.9.2b)
breadboards: 1

parts:
  R1 = Resistor [tolerance=±5% resistance=220 package=THT]
  R2 = Resistor [tolerance=±5% resistance=220 package=THT]
  S1 = Pushbutton [package="[THT]"]
  R4 = Resistor [tolerance=±5% resistance=10k package=THT]
  Componente1 = Arduino Uno (Rev3)
  LED1 = LED - 5mm [color="Green (570nm)" package="5 mm [THT]"]
  LED2 = LED - 5mm [color="Red (633nm)" package="5 mm [THT]"]

nets:
  N1: R1.Pin_0, LED2.anode
  N2: R1.Pin_1, Componente1.D2
  N3: R2.Pin_0, LED1.anode
  N4: R2.Pin_1, Componente1.D3_PWM
  N5: S1.Pin_1, S1.Pin_2, R4.Pin_1, Componente1.D7
  N6: S1.Pin_3, S1.Pin_4, Componente1.5V
  N7: R4.Pin_0, Componente1.GND, LED1.cathode, LED2.cathode

notes:
  Resistenze LED 220 Ohm
  Resistenza Tasto 10 Kohm
