# Fritzing sketch LED_RGB2_2017 (saved by Fritzing 0.9.2b)
breadboards: 1

parts:
  R1 = Resistor [tolerance=±5% resistance=220 package=THT]
  R2 = Resistor [tolerance=±5% resistance=220 package=THT]
  R3 = Resistor [tolerance=±5% resistance=220 package=THT]
  LED1 = RGB LED (com. cathode, rgb) [package="5 mm [THT]"]
  Componente1 = Arduino Uno (Rev3)
  S1 = Pushbutton [package="[THT]"]

nets:
  N1: R1.Pin_0, LED1.blue_anode
  N2: R1.Pin_1, Componente1.D3_PWM
  N3: R2.Pin_0, LED1.green_anode
  N4: R2.Pin_1, Componente1.D5_PWM
  N5: R3.Pin_0, LED1.red_anode
  N6: R3.Pin_1, Componente1.D6_PWM
  N7: LED1.common_cathode, Componente1.GND, S1.Pin_1, S1.Pin_2
  N8: Componente1.D8, S1.Pin_3, S1.Pin_4

notes:
  Resistenze LED 220 ohm
  ATTENZIONE !!!
  Tasto collegato SENZA
  resistenza di PULL_UP esterna da
  10 Kohm perchè nel codice è utilizzata la resistenza di
  PULL_UP interna.
  Codice:LED_RGB2.ino
  pinMode(Tasto, INPUT_PULLUP);
