# Fritzing sketch ANALOG_LM35DZ_LDR (saved by Fritzing 0.9.2b)
breadboards: 1

parts:
  R1 = Photocell (LDR) [package=THT]
  R2 = Resistor [tolerance=±5% resistance=10k package=THT]
  T1 = LM35 Temperature Sensor [package="TO92 [THT]"]
  LED1 = LED - 5mm [color="Red (633nm)" package="5 mm [THT]"]
  R3 = Resistor [tolerance=±5% resistance=220 package=THT]
  Componente1 = Arduino Uno (Rev3)

nets:
  N1: R1.pin_0, T1.+Vs, Componente1.5V
  N2: R1.pin_1, R2.Pin_0, Componente1.A0
  GND: R2.Pin_1, T1.GND, LED1.cathode, Componente1.GND
  N3: T1.Vout, Componente1.A1
  N4: LED1.anode, R3.Pin_0
  N5: R3.Pin_1, Componente1.D11_PWM/MOSI
