# Fritzing sketch LuxmetroLDR (saved by Fritzing 0.9.3b)
breadboards: 1

parts:
  LDR = Photocell (LDR) [package=THT]
  RPD_10KOhm = Resistor [tolerance=±5% resistance=220 package=THT]
  Componente1 = Arduino Uno (Rev3)

nets:
  N1: LDR.pin_0, Componente1.5V
  N2: LDR.pin_1, RPD_10KOhm.Pin_0, Componente1.A0
  N3: RPD_10KOhm.Pin_1, Componente1.GND
